# Fritzing sketch LED (saved by Fritzing 1.0.5)
breadboards: 1

parts:
  receiver = Arduino Nano (Rev3.0)
  sender = Arduino Nano (Rev3.0)
  LED1 = smd LED [color="Red (633nm)" package="0805 [SMD]"]
  R1 = Resistor [tolerance=±5% resistance=220 package="2512 [SMD]"]

nets:
  N1: receiver.D1/TX, sender.D0/RX
  N2: receiver.D0/RX, sender.D1/TX
  GND: receiver.GND, sender.GND, R1.Pin_1
  N3: sender.D13/SCK, LED1.anode
  N4: LED1.cathode, R1.Pin_0
