# Fritzing sketch LED_wiring (saved by Fritzing 1.0.5)
perfboards: 1

parts:
  R1 = Resistor [tolerance=±5% resistance=360k power=0.25W package=THT]
  R2 = Resistor [tolerance=±5% resistance=150k power=0.25W package=THT]
  C1 = Ceramic Capacitor [capacitance=470nF voltage=35V package="100 mil [THT, multilayer]"]
  LED1 = smd LED [color="Red (633nm)" package="0603 [SMD]"]
  LED2 = smd LED [color="Red (633nm)" package="0603 [SMD]"]
  R3 = Resistor [tolerance=±5% resistance=4.3k package="0402 [SMD]"]
  Vin = DC Power [voltage=5V internal_resistance=0.1Ω]
  元件1 = Arduino Nano (Rev3.0)

nets:
  N1: R1.Pin_0, Vin.V+
  N2: R1.Pin_1, R2.Pin_0, C1.0, C1.1, LED1.cathode, LED2.cathode, R3.Pin_0, Vin.V-, 元件1.GND, 元件1.A0
  N3: R2.Pin_1, R3.Pin_1
  N4: LED1.anode, 元件1.D10
  N5: LED2.anode, 元件1.D11/MOSI
