# Fritzing sketch Untitled_Sketch (saved by Fritzing 0.9.3b)
perfboards: 1

parts:
  R1 = Resistor [tolerance=±5% resistance=360k package=THT]
  R2 = Resistor [tolerance=±5% resistance=150k package=THT]
  C1 = Ceramic Capacitor [capacitance=22µF package="100 mil [THT, multilayer]"]
  LED1 = smd LED [color="Red (633nm)" package="0603 [SMD]"]
  LED2 = smd LED [color="Red (633nm)" package="0603 [SMD]"]
  R3 = Resistor [tolerance=±5% resistance=4.3k package="0402 [SMD]"]
  元件1 = Arduino Nano (Rev3.0)
  VCC1 = Battery

nets:
  N1: R1.Pin_0, VCC1.+
  N2: R1.Pin_1, R2.Pin_0, C1.0
  N3: R2.Pin_1, R3.Pin_1, VCC1.-
  N4: LED1.cathode, LED2.cathode, R3.Pin_0, 元件1.GND
  N5: LED1.anode, 元件1.D10
  N6: LED2.anode, 元件1.D11/MOSI
