# Fritzing sketch Untitled_Sketch_2 (saved by Fritzing 1.0.5)
breadboards: 1

parts:
  元件1 = Arduino Nano (Rev3.0)
  S1 = Pushbutton [package=THT]

nets:
  N1: 元件1.GND, S1.leg1
  N2: 元件1.D13/SCK, S1.leg0
